# Fritzing sketch prueba (saved by Fritzing 0.9.1b)
breadboards: 1

parts:
  U1 = GAS_SENSOR [package=mq-3]
  DHT1 = DHT11 Humitidy and Temperature Sensor
  Parte1 = Arduino Nano (Rev3.0)
  Raspberry_Pi1 = Raspberry Pi B rev2  # not connected

nets:
  N1: U1.B1, Parte1.A1
  GND: U1.H1, DHT1.GND, Parte1.GND
  VDD: U1.H2, DHT1.VDD, Parte1.5V
  N2: DHT1.DATA, Parte1.A0

notes:
  Conectar arduino nano por usb a raspberry en /descktop, node/prueba.js esta el lector de serial y escribinendo en firebase en tiempo real

custom parts:
  DHT11 Humitidy and Temperature Sensor: DHT11 Humidity and Temperature Sensor
